# Fritzing sketch ScienceFair2017-2018 (saved by Fritzing 0.9.3b)
breadboards: 1

parts:
  Part2 = Arduino Mega 2560 (Rev3)
  Grove1 = Grove OLED 128x96
  U1 = POT [package=pot_alpha_rv16af-20]
  U2 = POT [package=pot_alpha_rv16af-20]
  U3 = POT [package=pot_alpha_rv16af-20]
  M2 = Stepper Motor - Bipolar
  Pololu_A1 = Pololu A4988 [package=SO16]
  Pololu_A2 = Pololu A4988 [package=SO16]
  S2 = SPST Switch [package=switch-spst-smd-a]
  S3 = SPST Switch [package=switch-spst-smd-a]
  GPS1 = Adafruit Ultimate GPS Breakout
  M3 = Stepper Motor - Bipolar

nets:
  N1: Part2.A0, U2.S
  N2: Part2.A1, U3.S
  N3: Part2.A2, U1.S
  N4: Part2.D21/SCL, Grove1.SCL
  N5: Part2.D20/SDA, Grove1.SDA
  VDD: Part2.5V, Grove1.VCC, U1.E, U2.E, U3.E, Pololu_A1.VDD, Pololu_A2.VDD, GPS1.VIN
  GND: Part2.GND, Grove1.GND, U1.A, U2.A, U3.A, Pololu_A1.GND#8, Pololu_A2.GND#8, S2.O, S3.O, GPS1.GND
  N6: Part2.D2_PWM, GPS1.RX
  N7: Part2.D3_PWM, GPS1.TX
  N8: Part2.D4_PWM, Pololu_A2.DIR
  N9: Part2.D5_PWM, Pololu_A2.STEP
  N10: Part2.D6_PWM, Pololu_A1.DIR
  N11: Part2.D7_PWM, Pololu_A1.STEP
  N12: Part2.D50, S2.P
  N13: Part2.D51, S3.P
  N14: M2.A, Pololu_A1.2B
  N15: M2.C, Pololu_A1.2A
  N16: M2.B, Pololu_A1.1A
  N17: M2.D, Pololu_A1.1B
  N18: Pololu_A1.RESET, Pololu_A1.SLEEP
  N19: Pololu_A2.RESET, Pololu_A2.SLEEP
  N20: Pololu_A2.1B, M3.D
  N21: Pololu_A2.1A, M3.B
  N22: Pololu_A2.2A, M3.C
  N23: Pololu_A2.2B, M3.A
